# Fritzing sketch Esquematico (saved by Fritzing 0.9.3b)
breadboards: 1

parts:
  Raspberry_Pi_1 = Raspberry Pi 3 [part_number=RPI-3-V1.2]
  AM1 = AM2302 Humidity and Temperature Sensor
  Part1 = Adafruit FONA 808 Breakout [part_number="Adafruit #2542"]
  R1 = Resistor [tolerance=±5% resistance=10 package=THT]
  ANT1 = Antenna  # not connected
  U1 = U.FL [package=u.fl]
  Componente1 = RFID USB Reader
  S1 = Pushbutton [package="[THT]"]
  BAT1 = Battery Holders [package=lipo-1100mAh]

nets:
  3V3: Raspberry_Pi_1.3v3, Raspberry_Pi_1.3V3, AM1.VDD, Part1.Vio
  N1: Raspberry_Pi_1.GPIO2, Componente1.GND
  N2: Raspberry_Pi_1.GPIO3, Componente1.TX-O
  N3: Raspberry_Pi_1.GPIO4, Componente1.VCC
  GND: Raspberry_Pi_1.GND, AM1.GND, Part1.GND, Part1.Key, Componente1.ANT1, S1.Pin_1, S1.Pin_2, BAT1.-
  N4: Raspberry_Pi_1.GPIO17, S1.Pin_3, S1.Pin_4
  N5: Raspberry_Pi_1.GPIO23, AM1.DATA
  N6: Raspberry_Pi_1.GPIO15, Part1.TXD
  N7: Raspberry_Pi_1.GPIO14, Part1.RXD
  5V: Raspberry_Pi_1.5V, Part1.+5V, Componente1.TX-O-RS232
  N8: Part1.Bat, R1.Pin_0, BAT1.+
  N9: R1.Pin_1, U1.SIGNAL

custom parts:
  Adafruit FONA 808 Breakout: Cellular + GPS tracking, all in one? Oh yes! Introducing Adafruit FONA 808 MiniGSM + GPS, an all-in-one cellular phone module with that lets you add location-tracking, voice, text, SMS and data to your project in an adorable little package.
